# Fritzing sketch O tabuleiro do Genius (saved by Fritzing 0.9.3b)
breadboards: 1

parts:
  Part1 = Arduino Uno (Rev3)
  R1 = Resistor [tolerance=±5% resistance=220 package=THT]
  S1 = Pushbutton [package="[THT]"]
  LED1 = LED - 5mm [color="Green (555nm)" package="5 mm [THT]"]
  S2 = Pushbutton [package="[THT]"]
  S3 = Pushbutton [package="[THT]"]
  S4 = Pushbutton [package="[THT]"]
  LED2 = LED - 5mm [color="Red (633nm)" package="5 mm [THT]"]
  LED3 = LED - 5mm [color="Yellow (592nm)" package="5 mm [THT]"]
  LED4 = LED - 5mm [color="White (6500K)" package="5 mm [THT]"]
  R2 = Resistor [tolerance=±5% resistance=220 package=THT]
  R3 = Resistor [tolerance=±5% resistance=220 package=THT]
  R4 = Resistor [tolerance=±5% resistance=220 package=THT]

nets:
  N1: Part1.D8, S4.Pin_3, S4.Pin_4
  N2: Part1.D9_PWM, S3.Pin_3, S3.Pin_4
  N3: Part1.D10_PWM/SS, S2.Pin_3, S2.Pin_4
  N4: Part1.D11_PWM/MOSI, S1.Pin_3, S1.Pin_4
  N5: Part1.D2, LED4.anode
  N6: Part1.D3_PWM, LED3.anode
  N7: Part1.D4, LED2.anode
  N8: Part1.D5_PWM, LED1.anode
  N9: Part1.GND, R1.Pin_1, S1.Pin_1, S1.Pin_2, S2.Pin_1, S2.Pin_2, S3.Pin_1, S3.Pin_2, S4.Pin_1, S4.Pin_2, R2.Pin_1, R3.Pin_1, R4.Pin_1
  N10: R1.Pin_0, LED1.cathode
  N11: LED2.cathode, R2.Pin_0
  N12: LED3.cathode, R3.Pin_0
  N13: LED4.cathode, R4.Pin_0
